# Fritzing sketch lcd_int (saved by Fritzing 0.8.7b)
breadboards: 1

parts:
  Raspberry_Pi_B_rev1 = Raspberry Pi B rev2
  U1 = LCD-16X2 [package=lcd-16x2]
  R1 = Trimmer Potentiometer [maximum_resistance=10kΩ package=THT]

nets:
  5V: Raspberry_Pi_B_rev1.5V, U1.VDD, U1.K, R1.leg1
  GND: Raspberry_Pi_B_rev1.GND, U1.VSS, U1.R_W, U1.A, R1.leg2
  N1: Raspberry_Pi_B_rev1.GPIO_23, U1.DB6
  N2: Raspberry_Pi_B_rev1.GPIO_18, U1.DB7
  N3: Raspberry_Pi_B_rev1.GPIO_24, U1.DB5
  N4: Raspberry_Pi_B_rev1.GPIO_25, U1.DB4
  N5: Raspberry_Pi_B_rev1.GPIO_8, U1.E
  N6: Raspberry_Pi_B_rev1.GPIO_7, U1.RS
  N7: U1.VO, R1.wiper
