# Fritzing sketch tah_testbed_sch (saved by Fritzing 0.8.7b)
breadboards: 1

parts:
  Part1 = Arduino Leonardo (Rev3b)
  Raspberry_Pi_B_rev1 = Raspberry Pi B rev2
  U1 = 74HC4067 [package=ssop24]
  U2 = LCD-16X2 [package=lcd-16x2]
  R1 = Trimmer Potentiometer [maximum_resistance=10kΩ package=THT]
  S1 = Pushbutton [package="[THT]"]
  R2 = Resistor [tolerance=±5% resistance=220 package="0603 [SMD]"]
  J1 = Piezo Speaker
  R3 = Resistor [package="0402 [SMD]"]
  S2 = Pushbutton [package="[THT]"]
  R4 = Resistor [tolerance=±5% resistance=220 package="0603 [SMD]"]
  74LS151 = SO16 [chip_label=HCF4051 package=SO]

nets:
  N1: Part1.D2/SDA, U1.CHAN11
  N2: Part1.D3_PWM/SCL, Part1.SCL, U1.CHAN10
  N3: Part1.D4/A6, U1.CHAN9
  N4: Part1.D5_PWM, U1.CHAN8
  N5: Part1.D6_PWM/A7, U1.CHAN7
  N6: Part1.D7, U1.CHAN6
  VIN: Part1.VIN, Raspberry_Pi_B_rev1.3V3, U1.VCC, 74LS151.16
  N7: Part1.A0, 74LS151.4
  N8: Part1.A1, 74LS151.5
  N9: Part1.A2, 74LS151.2
  N10: Part1.A3, 74LS151.1
  N11: Part1.A4, 74LS151.15
  N12: Part1.A5, 74LS151.14
  N13: Part1.D8/A8, U1.CHAN5
  N14: Part1.D9_PWM/A9, U1.CHAN4
  N15: Part1.D10_PWM/A10, U1.CHAN3
  N16: Part1.D11_PWM, U1.CHAN2
  N17: Part1.D12/A11, U1.CHAN1
  N18: Part1.D13_PWM, U1.CHAN0
  N19: Raspberry_Pi_B_rev1.5V, S1.Pin_1, S1.Pin_2, S2.Pin_1
  N20: Raspberry_Pi_B_rev1.GPIO_2, U1.S0, 74LS151.11
  N21: Raspberry_Pi_B_rev1.GPIO_3, U1.S1, 74LS151.10
  GND: Raspberry_Pi_B_rev1.GND, U1.GND, U1.EN, R2.Pin_0, J1.pin2, R4.Pin_1, 74LS151.6, 74LS151.7, 74LS151.8
  N22: Raspberry_Pi_B_rev1.GPIO_23, U1.COM, 74LS151.3
  N23: Raspberry_Pi_B_rev1.GPIO_14, U1.S2, 74LS151.9
  N24: Raspberry_Pi_B_rev1.GPIO_15, U1.S3
  N25: Raspberry_Pi_B_rev1.GPIO_17, S1.Pin_4, R4.Pin_0
  N26: Raspberry_Pi_B_rev1.GPIO_18, U2.DB7
  N27: Raspberry_Pi_B_rev1.GPIO_27, R2.Pin_1, S2.Pin_3, S2.Pin_4
  N28: Raspberry_Pi_B_rev1.GPIO_4, U2.DB6
  N29: Raspberry_Pi_B_rev1.GPIO_24, U2.DB5
  N30: Raspberry_Pi_B_rev1.GPIO_25, U2.DB4
  N31: Raspberry_Pi_B_rev1.GPIO_11, R3.Pin_1
  N32: Raspberry_Pi_B_rev1.GPIO_8, U2.E
  N33: Raspberry_Pi_B_rev1.GPIO_7, U2.RS
  GND_2: U2.VSS, U2.K, R1.leg1
  N34: U2.VO, R1.leg2
  5V: U2.A, R1.wiper
  N35: J1.pin1, R3.Pin_0
